# Fritzing sketch Brouwerij (saved by Fritzing 0.7.12b)
breadboards: 1

parts:
  Raspberry_Pi1 = Raspberry Pi (Model B)  # not connected
  DS1 = DS18B20 1-Wire Temperature Sensor [part_number=DS18B20]
  Pi1 = Adafruit Pi Cobbler
  R3 = Resistor [tolerance=±5% resistance=1k package=THT]
  R1 = Resistor [tolerance=±5% resistance=4.7k package=THT]
  Q1 = NPN-Transistor [package="TO92 [THT]"]
  SSR = Relay [part_number=FRS1B-S package=THT]

nets:
  VDD: DS1.VDD, Pi1.3V3, R1.Pin_0
  N1: DS1.DQ, Pi1.#4, R1.Pin_1
  GND: DS1.GND, Pi1.GND, Q1.E
  +5V: Pi1.5V0, SSR.COIL1
  N2: Pi1.#18, R3.Pin_0
  N3: R3.Pin_1, Q1.B
  N4: Q1.C, SSR.COIL2

notes:
  DS18B20:
  GND (white)
  DQ (blue/white)
  VDD (orange/white)
  Brewgear-Pi, Homebrew brewery automation, 1
  This is actually a big SSR

custom parts:
  Raspberry Pi (Model B): Raspberry Pi Single-board Computer, Model B
  Adafruit Pi Cobbler: Adafruit Pi Cobbler GPIO Breakout for Raspberry Pi
